// Logisim project Exemplo_0502.circ as structural Verilog: 1 circuit, main circuit main
module main (
  input  b,
  input  a,
  output na_b
);

  wire nor_1_out;

  not nor_1 (nor_1_out, b);  // NOR_Gate
  nor nor_2 (na_b, nor_1_out, a);
endmodule
