// Logisim project Exemplo_0503.circ as structural Verilog: 1 circuit, main circuit main
module main (
  input  a,
  input  b,
  output a_nb
);

  wire nand_1_out;

  not nand_1 (nand_1_out, a);  // NAND_Gate
  nand nand_2 (a_nb, nand_1_out, b);
endmodule
