// Logisim project Exemplo_0504.circ as structural Verilog: 1 circuit, main circuit main
module main (
  input  a,
  input  b,
  output na_nb
);

  wire nor_1_out, nor_2_out, nor_3_out;

  not nor_1 (nor_1_out, a);  // NOR_Gate
  not nor_2 (nor_2_out, b);  // NOR_Gate
  nor nor_3 (nor_3_out, nor_1_out, nor_2_out);
  not nor_4 (na_nb, nor_3_out);  // NOR_Gate
endmodule
