// Logisim project Exemplo_0505.circ as structural Verilog: 1 circuit, main circuit main
module main (
  input  a,
  input  b,
  output na_nb
);

  wire nand_1_out, nand_2_out, nand_3_out;

  not nand_1 (nand_1_out, a);  // NAND_Gate
  not nand_2 (nand_2_out, b);  // NAND_Gate
  nand nand_3 (nand_3_out, nand_1_out, nand_2_out);
  not nand_4 (na_nb, nand_3_out);  // NAND_Gate
endmodule
