// Logisim project Exemplo_0506.circ as structural Verilog: 1 circuit, main circuit main
module main (
  input  a,
  input  b,
  output n_a_b
);

  wire nor_1_out, nor_2_out, nor_3_out;

  nor nor_1 (nor_1_out, a, b);
  nor nor_2 (nor_2_out, a, nor_1_out);
  nor nor_3 (nor_3_out, nor_1_out, b);
  nor nor_4 (n_a_b, nor_2_out, nor_3_out);
endmodule
