// Logisim project Exemplo_0702.circ as structural Verilog: 1 circuit, main circuit main
module main (
  input  a,
  input  b,
  input  select,
  output s0,
  output s1,
  output s
);

  nor nor_1 (s0, b, a);
  nand nand_1 (s1, b, a);
  Multiplexer #(.enable("false")) multiplexer_1 (.in0(s0), .in1(s1), .out(s), .sel(select));
endmodule
