// Logisim project Exemplo_0703.circ as structural Verilog: 1 circuit, main circuit main
module main (
  input  a,
  input  b,
  input  select__x,
  input  select_g__xg,
  output s0,
  output s1,
  output s,
  output s2,
  output s3
);

  wire multiplexer_1_out, multiplexer_2_out;

  and and_1 (s0, b, a);
  nand nand_1 (s1, b, a);
  or or_1 (s2, b, a);
  nor nor_1 (s3, b, a);
  Multiplexer #(.enable("false")) multiplexer_1 (.in0(s0), .in1(s1), .out(multiplexer_1_out), .sel(select__x));
  Multiplexer #(.enable("false")) multiplexer_2 (.in0(s2), .in1(s3), .out(multiplexer_2_out), .sel(select__x));
  Multiplexer #(.enable("false")) multiplexer_3 (
    .in0(multiplexer_1_out), .in1(multiplexer_2_out), .out(s), .sel(select_g__xg));

  // Notes on the sheet:
  //   sx
  //   sy
endmodule
