// Logisim project Exemplo_0704.circ as structural Verilog: 1 circuit, main circuit main
module main (
  input  a,
  input  b,
  input  c,
  input  d,
  input  [1:0] select_g__xg,
  output s0,
  output s1,
  output s,
  output s2,
  output s3
);

  xor xor_1 (s0, b, a);
  xnor xnor_1 (s1, b, a);
  or or_1 (s2, d, c);
  nor nor_1 (s3, d, c);
  Multiplexer #(.select(2), .enable("false")) multiplexer_1 (
    .in0(s0), .in1(s1), .in2(s2), .in3(s3), .out(s), .sel(select_g__xg));
endmodule
