// Logisim project Exemplo_0705.circ as structural Verilog: 1 circuit, main circuit main
module main (
  input  a,
  input  b,
  input  [2:0] select,
  output s
);

  wire and_1_out, nand_1_out, nor_1_out, not_1_out, not_2_out, or_1_out, xnor_1_out, xor_1_out;

  xor xor_1 (xor_1_out, b, a);
  xnor xnor_1 (xnor_1_out, b, a);
  and and_1 (and_1_out, b, a);
  nand nand_1 (nand_1_out, b, a);
  or or_1 (or_1_out, b, a);
  nor nor_1 (nor_1_out, b, a);
  not not_1 (not_1_out, b);
  not not_2 (not_2_out, a);
  Multiplexer #(.select(3), .enable("false")) multiplexer_1 (
    .in0(xor_1_out), .in1(xnor_1_out), .in2(and_1_out), .in3(nand_1_out), .in4(or_1_out), .in5(nor_1_out),
    .in6(not_1_out), .in7(not_2_out), .out(s), .sel(select));
endmodule
