// Logisim project Comparator_Equal.circ as structural Verilog: 2 circuits, main circuit main
module main (
  input  A,
  input  B,
  output S
);

  xnor xnor_1 (S, A, B);
endmodule

module Comparador5bits (
  input  in_1,
  input  A,
  input  in_3,
  input  in_4,
  input  in_5,
  input  in_6,
  input  in_7,
  input  B,
  input  in_9,
  input  in_10,
  output S
);

  wire main_1_s, main_2_s, main_3_s, main_4_s, main_5_s;

  main main_1 (.A(in_5), .B(in_10), .S(main_1_s));
  main main_2 (.A(in_4), .B(in_9), .S(main_2_s));
  main main_3 (.A(in_3), .B(B), .S(main_3_s));
  main main_4 (.A(A), .B(in_7), .S(main_4_s));
  main main_5 (.A(in_1), .B(in_6), .S(main_5_s));
  and and_1 (S, main_1_s, main_2_s, main_3_s, main_4_s, main_5_s);
endmodule
