// Logisim project ComplementoDe2.circ as structural Verilog: 3 circuits, main circuit HalfAdder
module HalfAdder (
  input  A,
  input  B,
  output S,
  output CarryOut
);

  and and_1 (CarryOut, A, B);
  xor xor_1 (S, A, B);
endmodule

module comp (
  input  A,
  input  B,
  input  CarryIn,
  output S,
  output CarryOut
);

  wire halfadder_1_carryout, halfadder_1_s, halfadder_2_carryout, not_1_out;

  not not_1 (not_1_out, A);
  HalfAdder halfadder_1 (.A(not_1_out), .B(B), .S(halfadder_1_s), .CarryOut(halfadder_1_carryout));
  HalfAdder halfadder_2 (.A(halfadder_1_s), .B(CarryIn), .S(S), .CarryOut(halfadder_2_carryout));
  or or_1 (CarryOut, halfadder_2_carryout, halfadder_1_carryout);
endmodule

module Complemento2_5bits (
  input  in_1,
  input  A,
  input  in_3,
  input  in_4,
  input  in_5,
  input  in_6,
  input  B,
  input  in_8,
  input  in_9,
  input  in_10,
  output out_11,
  output out_12,
  output out_13,
  output out_14,
  output out_15
);

  wire comp_2_carryout, comp_3_carryout, comp_4_carryout, comp_5_carryout;

  comp comp_1 (.A(in_1), .B(in_6), .CarryIn(comp_2_carryout), .S(out_11));  // open: CarryOut
  comp comp_2 (.A(A), .B(B), .CarryIn(comp_3_carryout), .S(out_12), .CarryOut(comp_2_carryout));
  comp comp_3 (.A(in_3), .B(in_8), .CarryIn(comp_4_carryout), .S(out_13), .CarryOut(comp_3_carryout));
  comp comp_4 (.A(in_4), .B(in_9), .CarryIn(comp_5_carryout), .S(out_14), .CarryOut(comp_4_carryout));
  comp comp_5 (.A(in_5), .B(in_10), .CarryIn(1'b0), .S(out_15), .CarryOut(comp_5_carryout));
endmodule
