// Logisim project FullAdder.circ as structural Verilog: 5 circuits, main circuit main
module main (
  input  A,
  input  B,
  input  CarryIn,
  output S,
  output CarryOut
);

  wire and_1_out, and_2_out, and_3_out, xor_1_out;

  xor xor_1 (xor_1_out, B, A);
  and and_1 (and_1_out, CarryIn, B);
  and and_2 (and_2_out, CarryIn, A);
  and and_3 (and_3_out, B, A);
  xor xor_2 (S, xor_1_out, CarryIn);
  or or_1 (CarryOut, and_1_out, and_2_out, and_3_out);
endmodule

module Sum4bits (
  input  A,
  input  in_2,
  input  in_3,
  input  in_4,
  input  B,
  input  in_6,
  input  in_7,
  input  in_8,
  output out_9,
  output out_10,
  output out_11,
  output out_12
);

  wire main_2_carryout, main_3_carryout, main_4_carryout;

  main main_1 (.A(A), .B(B), .CarryIn(main_2_carryout), .S(out_9));  // open: CarryOut
  main main_2 (.A(in_2), .B(in_6), .CarryIn(main_3_carryout), .S(out_10), .CarryOut(main_2_carryout));
  main main_3 (.A(in_3), .B(in_7), .CarryIn(main_4_carryout), .S(out_11), .CarryOut(main_3_carryout));
  main main_4 (.A(in_4), .B(in_8), .CarryIn(1'b0), .S(out_12), .CarryOut(main_4_carryout));
endmodule

module HalfAdder (
  input  A,
  input  B,
  output S,
  output CarryOut
);

  and and_1 (CarryOut, A, B);
  xor xor_1 (S, A, B);
endmodule

module FA_com_HA (
  input  A,
  input  B,
  input  CarryIn,
  output S,
  output CarryOut
);

  wire halfadder_1_carryout, halfadder_1_s, halfadder_2_carryout;

  HalfAdder halfadder_1 (.A(A), .B(B), .S(halfadder_1_s), .CarryOut(halfadder_1_carryout));
  HalfAdder halfadder_2 (.A(halfadder_1_s), .B(CarryIn), .S(S), .CarryOut(halfadder_2_carryout));
  or or_1 (CarryOut, halfadder_2_carryout, halfadder_1_carryout);
endmodule

module Sum4bits2 (
  input  A,
  input  in_2,
  input  in_3,
  input  in_4,
  input  B,
  input  in_6,
  input  in_7,
  input  in_8,
  output out_9,
  output out_10,
  output out_11,
  output out_12
);

  wire fa_com_ha_2_carryout, fa_com_ha_3_carryout, fa_com_ha_4_carryout;

  FA_com_HA fa_com_ha_1 (.A(A), .B(B), .CarryIn(fa_com_ha_2_carryout), .S(out_9));  // open: CarryOut
  FA_com_HA fa_com_ha_2 (
    .A(in_2), .B(in_6), .CarryIn(fa_com_ha_3_carryout), .S(out_10), .CarryOut(fa_com_ha_2_carryout));
  FA_com_HA fa_com_ha_3 (
    .A(in_3), .B(in_7), .CarryIn(fa_com_ha_4_carryout), .S(out_11), .CarryOut(fa_com_ha_3_carryout));
  FA_com_HA fa_com_ha_4 (.A(in_4), .B(in_8), .CarryIn(1'b0), .S(out_12), .CarryOut(fa_com_ha_4_carryout));
endmodule
