// Logisim project FullSubtractor.circ as structural Verilog: 5 circuits, main circuit main
module main (
  input  A,
  input  B,
  input  BorrowIn,
  output S,
  output BorrowOut
);

  wire and_1_out, and_2_out, and_3_out, not_1_out, not_2_out, xor_1_out;

  xor xor_1 (xor_1_out, B, A);
  and and_1 (and_1_out, BorrowIn, B);
  and and_2 (and_2_out, BorrowIn, not_1_out);
  not not_1 (not_1_out, A);
  and and_3 (and_3_out, B, not_2_out);
  not not_2 (not_2_out, A);
  xor xor_2 (S, xor_1_out, BorrowIn);
  or or_1 (BorrowOut, and_1_out, and_2_out, and_3_out);
endmodule

module Sub4bits (
  input  A,
  input  in_2,
  input  in_3,
  input  in_4,
  input  B,
  input  in_6,
  input  in_7,
  input  in_8,
  output out_9,
  output out_10,
  output out_11,
  output out_12
);

  wire main_2_borrowout, main_3_borrowout, main_4_borrowout;

  main main_1 (.A(A), .B(B), .BorrowIn(main_2_borrowout), .S(out_9));  // open: BorrowOut
  main main_2 (.A(in_2), .B(in_6), .BorrowIn(main_3_borrowout), .S(out_10), .BorrowOut(main_2_borrowout));
  main main_3 (.A(in_3), .B(in_7), .BorrowIn(main_4_borrowout), .S(out_11), .BorrowOut(main_3_borrowout));
  main main_4 (.A(in_4), .B(in_8), .BorrowIn(1'b0), .S(out_12), .BorrowOut(main_4_borrowout));
endmodule

module HalfSubtractor (
  input  A,
  input  B,
  output S,
  output BorrowOut
);

  wire not_1_out;

  not not_1 (not_1_out, A);
  xor xor_1 (S, A, B);
  and and_1 (BorrowOut, not_1_out, B);
endmodule

module FS_com_HS (
  input  A,
  input  B,
  input  BorrowIn,
  output S,
  output BorrowOut
);

  wire halfsubtractor_1_borrowout, halfsubtractor_1_s, halfsubtractor_2_borrowout;

  HalfSubtractor halfsubtractor_1 (.A(A), .B(B), .S(halfsubtractor_1_s), .BorrowOut(halfsubtractor_1_borrowout));
  HalfSubtractor halfsubtractor_2 (.A(halfsubtractor_1_s), .B(BorrowIn), .S(S), .BorrowOut(halfsubtractor_2_borrowout));
  or or_1 (BorrowOut, halfsubtractor_2_borrowout, halfsubtractor_1_borrowout);
endmodule

module Sub4bits2 (
  input  A,
  input  in_2,
  input  in_3,
  input  in_4,
  input  B,
  input  in_6,
  input  in_7,
  input  in_8,
  output out_9,
  output out_10,
  output out_11,
  output out_12
);

  wire fs_com_hs_2_borrowout, fs_com_hs_3_borrowout, fs_com_hs_4_borrowout;

  FS_com_HS fs_com_hs_1 (.A(A), .B(B), .BorrowIn(fs_com_hs_2_borrowout), .S(out_9));  // open: BorrowOut
  FS_com_HS fs_com_hs_2 (
    .A(in_2), .B(in_6), .BorrowIn(fs_com_hs_3_borrowout), .S(out_10), .BorrowOut(fs_com_hs_2_borrowout));
  FS_com_HS fs_com_hs_3 (
    .A(in_3), .B(in_7), .BorrowIn(fs_com_hs_4_borrowout), .S(out_11), .BorrowOut(fs_com_hs_3_borrowout));
  FS_com_HS fs_com_hs_4 (.A(in_4), .B(in_8), .BorrowIn(1'b0), .S(out_12), .BorrowOut(fs_com_hs_4_borrowout));
endmodule
