// Logisim project Exemplo_1102.circ as structural Verilog: 3 circuits, main circuit main
module main (
  input  Input,
  output out_2,
  output out_3,
  output out_4,
  output out_5,
  output out_6,
  output out_7,
  output out_8,
  output \Próximo_Estado ,
  output out_10
);

  wire clock_1_out;

  nextState nextstate_1 (.i(Input), .s0(out_2), .s1(out_5), .s2(out_6), .s02(out_3), .s12(out_4), .s22(out_7));
  Clock clock_1 (.out(clock_1_out));
  D_Flip_Flop d_ff_1 (.clk(clock_1_out), .D(out_3), .Q(out_2));  // open: Qn, preset, reset
  D_Flip_Flop d_ff_2 (.clk(clock_1_out), .D(out_4), .Q(out_5));  // open: Qn, preset, reset
  D_Flip_Flop d_ff_3 (.clk(clock_1_out), .D(out_7), .Q(out_6));  // open: Qn, preset, reset

  assign out_8 = out_2;
  assign out_10 = out_6;
  assign \Próximo_Estado  = out_5;

  // Notes on the sheet:
  //   100 : Estado FINAL
  //   000: Estado INICIAL
endmodule

module \output  (
  input  s0,
  input  s1,
  input  s2,
  output S
);

  wire not_1_out, not_2_out, not_3_out;

  not not_1 (not_1_out, s0);
  not not_2 (not_2_out, s1);
  not not_3 (not_3_out, s2);
  and and_1 (S, not_1_out, not_2_out, not_3_out);
endmodule

module nextState (
  input  i,
  input  s0,
  input  s1,
  input  s2,
  output s02,
  output s12,
  output s22
);

  wire and_1_out, and_2_out, and_3_out, and_4_out, and_5_out, and_6_out, and_7_out, and_8_out, not_1_out,
       not_2_out, not_3_out, not_4_out, not_5_out, not_6_out, not_7_out, not_8_out, not_9_out, not_10_out,
       not_11_out, not_12_out;

  not not_1 (not_1_out, i);
  and and_1 (and_1_out, not_1_out, s1, s2);
  not not_2 (not_2_out, i);
  not not_3 (not_3_out, s1);
  not not_4 (not_4_out, i);
  not not_5 (not_5_out, s0);
  not not_6 (not_6_out, s2);
  not not_7 (not_7_out, i);
  and and_2 (and_2_out, not_7_out, s0, s2);
  not not_8 (not_8_out, i);
  and and_3 (and_3_out, not_8_out, s0, s1);
  and and_4 (and_4_out, i, not_9_out, not_10_out);
  not not_9 (not_9_out, s0);
  not not_10 (not_10_out, s1);
  and and_5 (and_5_out, i, not_11_out, not_12_out);
  not not_11 (not_11_out, s0);
  not not_12 (not_12_out, s2);
  or or_1 (s02, and_1_out, s0);
  and and_6 (and_6_out, not_2_out, not_3_out, s2);
  or or_2 (s12, and_6_out, and_7_out, and_8_out);
  and and_7 (and_7_out, not_4_out, s0, s1);
  and and_8 (and_8_out, i, not_5_out, s1, not_6_out);
  or or_3 (s22, and_2_out, and_3_out, and_4_out, and_5_out);
endmodule
